# Fritzing sketch gardentron (saved by Fritzing 0.9.6b)
breadboards: 1

parts:
  Mod1 = Raspberry Pi Pico
  SparkFun_BabyBuck_Regulator_5V = Voltage Regulator [package=to-220-alt]
  V1 = DC Power [voltage=12V]
  Relay_1 = RELAY [package=relay-jzc]
  Relay_2 = RELAY [package=relay-jzc]
  Relay_3 = RELAY [package=relay-jzc]
  Soil_sensor_1 = Trimmer Potentiometer [maximum_resistance=10kΩ package=THT]
  Soil_sensor_2 = Trimmer Potentiometer [package=THT]
  Soil_sensor_3 = Trimmer Potentiometer [maximum_resistance=10kΩ package=THT]

nets:
  N1: Mod1.pin_1, Relay_1.COIL1
  N2: Mod1.pin_2, Relay_2.COIL1
  N3: Mod1.pin_3, Mod1.pin_8, Mod1.pin_13, Mod1.pin_18, Mod1.pin_23, Mod1.pin_28, Mod1.pin_33, Mod1.pin_38, SparkFun_BabyBuck_Regulator_5V.GND, V1.V-, Relay_1.COIL2, Relay_2.COIL2, Relay_3.COIL2
  N4: Mod1.pin_4, Relay_3.COIL1
  N5: Mod1.pin_31, Soil_sensor_3.wiper
  N6: Mod1.pin_32, Soil_sensor_2.wiper
  N7: Mod1.pin_34, Soil_sensor_1.wiper
  N8: Mod1.pin_39, SparkFun_BabyBuck_Regulator_5V.OUT, Soil_sensor_1.leg2, Soil_sensor_2.leg2, Soil_sensor_3.leg2
  N9: SparkFun_BabyBuck_Regulator_5V.IN, V1.V+
  N10: Soil_sensor_1.leg1, Soil_sensor_2.leg1, Soil_sensor_3.leg1

custom parts:
  Raspberry Pi Pico: Raspberry Pi Pico. Based around the RP2040 microcontroller the Pico is a low cost microcontroller device bringing Raspberry Pi quality, cost, and easy of use to the microcontroller space. Jan 2021, Split part in to two versions: tht (this one) and SMD. This one will drill holes for a .1 in header in pcb to allow plugging in the module as well as providing pads to solder the module to the top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
